// Logisim project sim.circ as structural Verilog: 4 circuits, main circuit main
module main (
  input  [7:0] in_1,
  input  [3:0] in_2,
  output out_3
);

  wire [6:0] hamming_7_4_1_out_2;
  wire [8:8] parity_8bit_1_out_2;

  parity_8bit parity_8bit_1 (.in_1(in_1), .out_2(parity_8bit_1_out_2[8]));
  parity_check parity_check_1 (.in_1({parity_8bit_1_out_2[8], in_1}), .out_2(out_3));
  // Probe on hamming_7_4_1_out_2
  hamming_7_4 hamming_7_4_1 (.in_1(in_2), .out_2(hamming_7_4_1_out_2));
endmodule

module parity_8bit (
  input  [7:0] in_1,
  output out_2
);

  wire xor_1_out, xor_2_out, xor_3_out, xor_4_out, xor_5_out, xor_7_out;

  xor xor_1 (xor_1_out, in_1[0], in_1[1]);
  xor xor_2 (xor_2_out, in_1[2], in_1[3]);
  xor xor_3 (xor_3_out, in_1[4], in_1[5]);
  xor xor_4 (xor_4_out, in_1[6], in_1[7]);
  xor xor_5 (xor_5_out, xor_1_out, xor_2_out);
  xor xor_6 (out_2, xor_5_out, xor_7_out);
  xor xor_7 (xor_7_out, xor_3_out, xor_4_out);
endmodule

module parity_check (
  input  [8:0] in_1,
  output out_2
);

  wire parity_8bit_1_out_2;

  parity_8bit parity_8bit_1 (.in_1(in_1[7:0]), .out_2(parity_8bit_1_out_2));
  xnor xnor_1 (out_2, parity_8bit_1_out_2, in_1[8]);
endmodule

module hamming_7_4 (
  input  [3:0] in_1,
  output [6:0] out_2
);

  wire xor_1_out, xor_2_out, xor_3_out;

  xor xor_1 (xor_1_out, in_1[0], in_1[2]);
  xor xor_2 (xor_2_out, in_1[1], in_1[2]);
  xor xor_3 (xor_3_out, in_1[0], in_1[1]);
  xor xor_4 (out_2[0], xor_3_out, in_1[3]);
  xor xor_5 (out_2[1], xor_1_out, in_1[3]);
  xor xor_6 (out_2[2], xor_2_out, in_1[3]);

  assign out_2[6:3] = in_1;
endmodule
